// Digital circuit control_unit.dig as structural Verilog
module control_unit (
  input  [1:0] mode,
  input  irq,
  input  I_f,
  input  N_f,
  input  V_f,
  input  Z_f,
  input  C_f,
  input  clk,
  input  [7:0] opcode,
  output XFER_ASSERT_4,
  output XFER_LOAD_0,
  output EXT_FLIP,
  output RST_USEQ,
  output CLR_RST,
  output BRK,
  output ALU_OP_4,
  output DBUS_LOAD_3,
  output DBUS_ASSERT_0,
  output DBUS_ASSERT_1,
  output DBUS_ASSERT_2,
  output DBUS_ASSERT_3,
  output DBUS_LOAD_0,
  output DBUS_LOAD_1,
  output DBUS_LOAD_2,
  output ALU_OP_0,
  output ALU_OP_1,
  output ALU_OP_2,
  output ALU_OP_3,
  output XFER_ASSERT_0,
  output XFER_ASSERT_1,
  output XFER_ASSERT_2,
  output XFER_ASSERT_3,
  output XFER_LOAD_1,
  output ADDR_ASSERT_0,
  output ADDR_ASSERT_1,
  output ADDR_ASSERT_2,
  output COUNT_INC_0,
  output COUNT_INC_1,
  output COUNT_INC_2,
  output COUNT_DEC_0,
  output COUNT_DEC_1
);

  wire sequencer_p1, sequencer_p2, sequencer_p4, sequencer_p5, sequencer_p6, sequencer_p11, sequencer_p12,
       sequencer_p16;
  wire [2:0] t_state;
  wire [7:0] opcode_t, ucode_2_d, ucode_3_d, ucode_4_d, ucode_d;

  // _74193 sequencer: pin names not known; wires that end beside it: sequencer_p1, sequencer_p2, clk, sequencer_p4, sequencer_p5, sequencer_p6, RST_USEQ, 1'b1, 1'b1, 1'b0, sequencer_p11, sequencer_p12, t_state[0], t_state[1], t_state[2], sequencer_p16
  // NotConnected on sequencer_p1
  // NotConnected on sequencer_p2
  // NotConnected on sequencer_p4
  // NotConnected on sequencer_p5
  // NotConnected on sequencer_p6
  // NotConnected on sequencer_p11
  // NotConnected on sequencer_p12
  // NotConnected on sequencer_p16
  EEPROM #(.AddrBits(19), .Bits(8)) ucode (
    .A({mode, irq, opcode_t, C_f, Z_f, V_f, N_f, I_f, t_state}), .CS(1'b1), .WE(1'b0), .OE(1'b1), .D(ucode_d));
  EEPROM #(.AddrBits(19), .Bits(8)) ucode_2 (
    .A({mode, irq, opcode_t, C_f, Z_f, V_f, N_f, I_f, t_state}), .CS(1'b1), .WE(1'b0), .OE(1'b1),
    .D(ucode_2_d));
  _74ls574 _74ls574_1 (
    .nOC(1'b0), .CLK(clk), .D(ucode_d), .VCC(1'b1), .GND(1'b0),
    .Q({XFER_ASSERT_2, XFER_ASSERT_1, XFER_ASSERT_0, ALU_OP_4, ALU_OP_3, ALU_OP_2, ALU_OP_1, ALU_OP_0}));
  _74ls574 _74ls574_2 (
    .nOC(1'b0), .CLK(clk), .D(ucode_2_d), .VCC(1'b1), .GND(1'b0),
    .Q({DBUS_LOAD_3, DBUS_LOAD_2, DBUS_LOAD_1, DBUS_LOAD_0, DBUS_ASSERT_3, DBUS_ASSERT_2, DBUS_ASSERT_1, DBUS_ASSERT_0}));
  EEPROM #(.AddrBits(19), .Bits(8)) ucode_3 (
    .A({mode, irq, opcode_t, C_f, Z_f, V_f, N_f, I_f, t_state}), .CS(1'b1), .WE(1'b0), .OE(1'b1),
    .D(ucode_3_d));
  EEPROM #(.AddrBits(19), .Bits(8)) ucode_4 (
    .A({mode, irq, opcode_t, C_f, Z_f, V_f, N_f, I_f, t_state}), .CS(1'b1), .WE(1'b0), .OE(1'b1),
    .D(ucode_4_d));
  _74ls574 _74ls574_3 (
    .nOC(1'b0), .CLK(clk), .D(ucode_3_d), .VCC(1'b1), .GND(1'b0),
    .Q({BRK, CLR_RST, RST_USEQ, EXT_FLIP, COUNT_DEC_1, COUNT_DEC_0, COUNT_INC_2, COUNT_INC_1}));
  _74ls574 _74ls574_4 (
    .nOC(1'b0), .CLK(clk), .D(ucode_4_d), .VCC(1'b1), .GND(1'b0),
    .Q({COUNT_INC_0, ADDR_ASSERT_2, ADDR_ASSERT_1, ADDR_ASSERT_0, XFER_LOAD_1, XFER_LOAD_0, XFER_ASSERT_4, XFER_ASSERT_3}));

  // Other names for the same wires on the sheet: ucode_addr[18:0] = {mode, irq, opcode_t, C_f, Z_f, V_f, N_f, I_f, t_state};
  //   c_flag = C_f; i_flag = I_f; n_flag = N_f; opcoode[7:0] = opcode; v_flag = V_f; z_flag = Z_f
endmodule
